# Fritzing sketch Prototype (saved by Fritzing 0.9.3b)
circuit board: 6.88566cm x 5.36311cm

parts:
  Part1 = Arduino Uno (Rev3) - ICSP
  Part2 = Adafruit TCA9548A
  JP1 = Header 4 [package=jst-4-pth]
  JP2 = Header 4 [package=jst-4-pth]
  JP3 = Header 4 [package=jst-4-pth]
  JP4 = Header 4 [package=jst-4-pth]
  JP5 = Header 4 [package=jst-4-pth]
  JP6 = Header 4 [package=jst-4-pth]
  JP7 = Header 4 [package=jst-4-pth]
  JP8 = Header 4 [package=jst-4-pth]
  JP10 = Header 4 [package=jst-4-pth]
  JP11 = Header 4 [package=jst-4-pth]
  JP12 = Header 4 [package=jst-4-pth]
  R1 = Resistor [tolerance=±5% resistance=10k package="1206 [SMD]"]
  R2 = Resistor [tolerance=±5% resistance=10k package="1206 [SMD]"]
  JP13 = Header 4 [package=jst-4-pth]
  R3 = Resistor [tolerance=±5% resistance=10k package="1206 [SMD]"]
  R4 = Resistor [tolerance=±5% resistance=10k package="1206 [SMD]"]
  R5 = Resistor [tolerance=±5% resistance=10k package="1206 [SMD]"]
  R6 = Resistor [tolerance=±5% resistance=10k package="1206 [SMD]"]
  R7 = Resistor [tolerance=±5% resistance=10k package="1206 [SMD]"]
  R8 = Resistor [tolerance=±5% resistance=10k package="1206 [SMD]"]
  R10 = Resistor [tolerance=±5% resistance=10k package="1206 [SMD]"]
  R9 = Resistor [tolerance=±5% resistance=10k package="1206 [SMD]"]
  R11 = Resistor [tolerance=±5% resistance=10k package="1206 [SMD]"]
  R12 = Resistor [tolerance=±5% resistance=10k package="1206 [SMD]"]
  R13 = Resistor [tolerance=±5% resistance=10k package="1206 [SMD]"]
  R14 = Resistor [tolerance=±5% resistance=10k package="1206 [SMD]"]
  JP9 = Header 4 [package=jst-4-pth]

nets:
  N1: Part1.A4/SDA, Part2.INPUTSDA
  N2: Part1.A5/SCL, Part2.INPUTSCL
  N3: Part1.ICSP_MISO, Part1.D12/MISO, JP2.2
  5V: Part1.5V, Part2.VCC, JP1.1, JP2.1, JP3.1, JP4.1, JP5.1, JP6.1, JP7.2, JP8.2, JP10.2, JP11.2, JP12.2, R1.Pin_1, R2.Pin_1, JP13.2, R3.Pin_1, R4.Pin_1, R5.Pin_1, R6.Pin_1, R7.Pin_1, R8.Pin_1, R10.Pin_1, R9.Pin_1, R11.Pin_1, R12.Pin_1, R13.Pin_1, R14.Pin_1, JP9.2
  N4: Part1.ICSP_MOSI, Part1.D11_PWM/MOSI, JP1.3
  GND: Part1.GND, Part2.GND, JP1.4, JP2.4, JP3.4, JP4.4, JP5.4, JP6.4, JP7.3, JP8.3, JP10.3, JP11.3, JP12.3, JP13.3, JP9.3
  N5: Part1.D8, JP3.2
  N6: Part1.D9_PWM, JP3.3
  N7: Part1.D10_PWM/SS, JP1.2
  N8: Part1.D13/SCK, JP2.3
  N9: Part1.D2, JP4.2
  N10: Part1.D3_PWM, JP4.3
  N11: Part1.D4, JP6.2
  N12: Part1.D5_PWM, JP6.3
  N13: Part1.D6_PWM, JP5.2
  N14: Part1.D7, JP5.3
  N15: Part2.2SDA, JP8.4, R10.Pin_0
  N16: Part2.2SCL, JP8.1, R9.Pin_0
  N17: Part2.3SDA, JP12.4, R6.Pin_0
  N18: Part2.3SCL, JP12.1, R5.Pin_0
  N19: Part2.4SDA, JP10.4, R4.Pin_0
  N20: Part2.4SCL, JP10.1, R3.Pin_0
  N21: Part2.5SDA, R1.Pin_0, JP13.4
  N22: Part2.5SCL, R2.Pin_0, JP13.1
  N23: Part2.6SDA, JP11.4, R8.Pin_0
  N24: Part2.6SCL, JP11.1, R7.Pin_0
  N25: Part2.0SDA, R11.Pin_0, JP9.4
  N26: Part2.0SCL, R12.Pin_0, JP9.1
  N27: Part2.1SDA, JP7.4, R13.Pin_0
  N28: Part2.1SCL, JP7.1, R14.Pin_0

notes:
  Dimitar R.
  REV'IT!
  LAB
  v. 0.0.1
  nov 2019

custom parts:
  Adafruit TCA9548A: You just found the perfect I2C sensor, and you want to wire up two or three or more of them to your Arduino when you realize "Uh oh, this chip has a fixed I2C address, and from what I know about I2C, you cannot have two devices with the same address on the same SDA/SCL pins!" Are you out of luck? You would be, if you didn't have this ultra-cool TCA9548A 1-to-8 I2C multiplexer! Finally, a way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
